// Logisim project problem 2 q 2.circ as structural Verilog: 1 circuit, main circuit main
module main (
  input  a,
  input  b,
  input  c,
  output x
);

  wire and_1_out, and_2_out, and_3_out, not_1_out, not_2_out, not_3_out, not_4_out, not_5_out, not_6_out,
       not_7_out, or_1_out;

  not not_1 (not_1_out, a);
  not not_2 (not_2_out, c);
  not not_3 (not_3_out, b);
  not not_4 (not_4_out, c);
  not not_5 (not_5_out, a);
  not not_6 (not_6_out, b);
  not not_7 (not_7_out, c);
  and and_1 (and_1_out, not_1_out, b, not_2_out);
  and and_2 (and_2_out, a, not_3_out, not_4_out);
  and and_3 (and_3_out, not_5_out, not_6_out, not_7_out);
  or or_1 (or_1_out, and_1_out, and_2_out, and_3_out);
  and and_4 (x, or_1_out, a, b);
endmodule
