// Logisim project problem 2 q 3.circ as structural Verilog: 1 circuit, main circuit main
module main (
  input  a,
  input  b,
  input  c,
  output x
);

  wire and_1_out, and_2_out, and_3_out, and_4_out, not_1_out, not_2_out;

  not not_1 (not_1_out, c);
  not not_2 (not_2_out, c);
  and and_1 (and_1_out, a, b);
  and and_2 (and_2_out, a, b, not_1_out);
  and and_3 (and_3_out, a, b, not_2_out);
  and and_4 (and_4_out, a, b, c);
  or or_1 (x, and_1_out, and_2_out, and_3_out, and_4_out);
endmodule
