// Logisim project problem 3 q 3.circ as structural Verilog: 1 circuit, main circuit main
module main (
  input  a,
  input  b,
  input  c,
  output x
);

  wire not_1_out, not_2_out, not_3_out, not_4_out, or_1_out, or_2_out, or_3_out, or_4_out;

  not not_1 (not_1_out, b);
  not not_2 (not_2_out, c);
  not not_3 (not_3_out, c);
  not not_4 (not_4_out, b);
  or or_1 (or_1_out, a, b, c);
  or or_2 (or_2_out, a, not_1_out, not_2_out);
  or or_3 (or_3_out, a, b, not_3_out);
  or or_4 (or_4_out, a, not_4_out, c);
  and and_1 (x, or_1_out, or_2_out, or_3_out, or_4_out);
endmodule
