// Logisim project problem 4 q 2.circ as structural Verilog: 1 circuit, main circuit main
module main (
  input  a,
  input  b,
  input  c,
  output x
);

  wire not_1_out, not_2_out, or_1_out, or_2_out, or_3_out;

  not not_1 (not_1_out, a);
  not not_2 (not_2_out, b);
  or or_1 (or_1_out, a, b);
  or or_2 (or_2_out, a, c);
  or or_3 (or_3_out, not_1_out, not_2_out);
  and and_1 (x, or_1_out, or_2_out, or_3_out);
endmodule
