// Logisim project problem 4 q 3.circ as structural Verilog: 1 circuit, main circuit main
module main (
  input  a,
  input  b,
  input  c,
  output x
);

  wire and_1_out, and_2_out;

  and and_1 (and_1_out, a, b);
  and and_2 (and_2_out, a, c);
  or or_1 (x, and_1_out, and_2_out);
endmodule
